// Logisim project exception.circ as structural Verilog: 8 circuits, main circuit main
module main (
  input  in_1,
  output [3:0] Statev
);

  wire alu_1_equal_flag, ALUSrcA, and_1_out, Branch, CauseWrite, clk, EPCWrite, IntCause, IoD, IrWrite,
       MemtoReg, MemWrite, not_1_out, or_1_out, PCWrite, RegDst, RegWrite, undriven;
  wire [1:0] ALUOp, ALUSrcB, PCSrc;
  wire [4:0] multiplexer_3_out, reg_splitter_1__11_15, reg_splitter_1__16_20, reg_splitter_1__21_25;
  wire [5:0] fncd, Opd;
  wire [15:0] reg_splitter_1__0_15;
  wire [25:0] var1;
  wire [31:0] A_q, alu_1_output, B_3_q, bit_extender_1_out, bit_extender_2_out, multiplexer_1_out,
       multiplexer_2_out, multiplexer_4_out, multiplexer_5_out, multiplexer_6_out, multiplexer_7_out,
       ram_1_data, register_1_q, register_2_q, register_3_q, register_4_q, register_file_1_rd1___output_0,
       register_file_1_rd2___output_1;

  Clock clock_1 (.out(clk));
  Register #(.width(32)) register_1 (.D(multiplexer_7_out), .en(or_1_out), .Q(register_1_q), .clk(clk), .clr(in_1));
  control control_1 (
    .controlclock(clk), .Opcode(Opd), .Clear(in_1), .Statev(Statev), .RegWrite(RegWrite), .ALUSrcA(ALUSrcA),
    .ALUSrcB(ALUSrcB), .ALUOp(ALUOp), .PCSrc(PCSrc), .Branch(Branch), .PcWrite(PCWrite), .MemtoReg(MemtoReg),
    .RegDst(RegDst), .IRwrite(IrWrite), .MemWrite(MemWrite), .IoD(IoD));
  Register #(.width(32)) B (.D(register_1_q), .en(EPCWrite), .clk(clk), .clr(in_1));  // open: Q
  Multiplexer #(.width(32)) multiplexer_1 (
    .in0(register_1_q), .in1(register_4_q), .out(multiplexer_1_out), .sel(IoD));  // open: en
  Multiplexer #(.width(32)) multiplexer_2 (
    .in0(32'h30), .in1(32'h28), .out(multiplexer_2_out), .sel(IntCause), .en(undriven));
  not not_1 (not_1_out, MemWrite);
  Register #(.width(32)) B_2 (.D(multiplexer_2_out), .en(CauseWrite), .clk(clk), .clr(in_1));  // open: Q
  RAM #(.addrWidth(24), .dataWidth(32), .bus("separate")) ram_1 (
    .addr(multiplexer_1_out[23:0]), .din(B_3_q), .data(ram_1_data), .str(MemWrite), .sel(1'b1), .clk(clk),
    .ld(not_1_out));  // open: clr
  Register #(.width(32)) register_2 (.D(ram_1_data), .en(IrWrite), .Q(register_2_q), .clk(clk), .clr(in_1));
  Register #(.width(32)) register_3 (.D(ram_1_data), .Q(register_3_q), .clk(clk));  // open: en, clr
  Reg_Splitter reg_splitter_1 (
    .in_1(register_2_q), ._0_5(fncd), ._26_31(Opd), ._0_25(var1), ._21_25(reg_splitter_1__21_25),
    ._16_20(reg_splitter_1__16_20), ._11_15(reg_splitter_1__11_15), ._0_15(reg_splitter_1__0_15));
  Multiplexer #(.width(5)) multiplexer_3 (
    .in0(reg_splitter_1__16_20), .in1(reg_splitter_1__11_15), .out(multiplexer_3_out), .sel(RegDst));  // open: en
  Multiplexer #(.width(32)) multiplexer_4 (
    .in0(register_4_q), .in1(register_3_q), .out(multiplexer_4_out), .sel(MemtoReg));  // open: en
  Register_File register_file_1 (
    .A1___Output_0_Address(reg_splitter_1__21_25), .A2___Output_1_Address(reg_splitter_1__16_20),
    .A3___Write_Address(multiplexer_3_out), .WD3___Write_Value(multiplexer_4_out), .CLK___Clock(clk),
    .WE3___Write_Enable(RegWrite), .clear(in_1), .RD1___Output_0(register_file_1_rd1___output_0),
    .RD2___Output_1(register_file_1_rd2___output_1));
  assign bit_extender_1_out = {{16{reg_splitter_1__0_15[15]}}, reg_splitter_1__0_15};  // Bit_Extender bit_extender_1
  Register #(.width(32)) A (.D(register_file_1_rd1___output_0), .Q(A_q), .clk(clk), .clr(in_1));  // open: en
  Register #(.width(32)) B_3 (.D(register_file_1_rd2___output_1), .Q(B_3_q), .clk(clk), .clr(in_1));  // open: en
  Multiplexer #(.width(32)) multiplexer_5 (
    .in0(register_1_q), .in1(A_q), .out(multiplexer_5_out), .sel(ALUSrcA));  // open: en
  Multiplexer #(.select(2), .width(32)) multiplexer_6 (
    .in0(B_3_q), .in1(32'h1), .in2(bit_extender_1_out), .in3(bit_extender_1_out), .out(multiplexer_6_out),
    .sel(ALUSrcB));  // open: en
  ALU alu_1 (
    .Aluop(ALUOp), .fncd(fncd), .A(multiplexer_5_out), .B(multiplexer_6_out), .IntCause(IntCause),
    .EPCWrite(EPCWrite), .CauseWrite(CauseWrite), .Output(alu_1_output), .Equal_Flag(alu_1_equal_flag));
  and and_1 (and_1_out, Branch, alu_1_equal_flag);
  Register #(.width(32)) register_4 (.D(alu_1_output), .Q(register_4_q), .clk(clk), .clr(in_1));  // open: en
  assign bit_extender_2_out = {{6{var1[25]}}, var1};  // Bit_Extender bit_extender_2
  or or_1 (or_1_out, PCWrite, and_1_out);
  Multiplexer #(.select(2), .width(32)) multiplexer_7 (
    .in0(alu_1_output), .in1(register_4_q), .in2(bit_extender_2_out), .in3(bit_extender_2_out),
    .out(multiplexer_7_out), .sel(PCSrc));  // open: en
endmodule

module Reg_Splitter (
  input  [31:0] in_1,
  output [25:0] _0_25,
  output [4:0] _21_25,
  output [4:0] _16_20,
  output [4:0] _11_15,
  output [5:0] _26_31,
  output [5:0] _0_5,
  output [15:0] _0_15
);


  assign _0_5 = in_1[5:0];
  assign _0_15 = in_1[15:0];
  assign _0_25 = in_1[25:0];
  assign _11_15 = in_1[15:11];
  assign _16_20 = in_1[20:16];
  assign _21_25 = in_1[25:21];
  assign _26_31 = in_1[31:26];
endmodule

module control (
  input  controlclock,
  input  Clear,
  input  [5:0] Opcode,
  output [3:0] Statev,
  output RegWrite,
  output ALUSrcA,
  output [1:0] ALUSrcB,
  output [1:0] ALUOp,
  output [1:0] PCSrc,
  output Branch,
  output PcWrite,
  output MemtoReg,
  output RegDst,
  output IRwrite,
  output MemWrite,
  output IoD
);

  wire [0:0] multiplexer_2_out;
  wire [3:0] control_unit_1_out_4, multiplexer_1_out, multiplexer_3_out;

  control_unit control_unit_1 (
    .op_1(Opcode[5]), .op_2(Opcode[4]), .op_3(Opcode[3]), .op_4(Opcode[2]), .op_5(Opcode[1]),
    .op_6(Opcode[0]), .out_1(control_unit_1_out_4[3]), .out_2(control_unit_1_out_4[2]),
    .out_3(control_unit_1_out_4[1]), .out_4(control_unit_1_out_4[0]));
  Multiplexer #(.width(4)) multiplexer_1 (
    .in0(4'b0011), .in1(4'b0101), .out(multiplexer_1_out), .sel(Opcode[3]));  // open: en
  Multiplexer #(.select(4), .width(16)) multiplexer_2 (
    .in0(16'h2408), .in1(16'h18), .in2(16'h14), .in3(16'h8000), .in4(16'h802), .in5(16'hc000), .in6(16'h44),
    .in7(16'h1002), .in8(16'h2a4), .in9(16'h14), .in10(16'h2), .in11(16'h500), .in12(16'h14), .in13(16'h14),
    .out({IoD, MemWrite, IRwrite, RegDst, MemtoReg, PcWrite, Branch, PCSrc, ALUOp, ALUSrcB, ALUSrcA, RegWrite, multiplexer_2_out[0]}),
    .sel(Statev));  // open: in14, in15, en
  Multiplexer #(.select(4), .width(4)) multiplexer_3 (
    .in0(4'b0001), .in1(control_unit_1_out_4), .in2(multiplexer_1_out), .in3(4'b0100), .in4(4'b0000),
    .in5(4'b0000), .in6(4'b0111), .in7(4'b0000), .in8(4'b0000), .in9(4'b1010), .in10(4'b0000),
    .in11(4'b0000), .in12(4'b1010), .in13(4'b1010), .out(multiplexer_3_out), .sel(Statev));  // open: in14, in15, en
  Register #(.width(4)) register_1 (.D(multiplexer_3_out), .Q(Statev), .clk(controlclock), .clr(Clear));  // open: en
endmodule

module ALUcontrol (
  input  op5,
  input  op4,
  input  op3,
  input  op2,
  input  op1,
  input  op0,
  output s3,
  output s2,
  output s1,
  output s0
);

  wire and_2_out, and_3_out, not_1_out, not_2_out, not_3_out, not_4_out, not_5_out, not_6_out, not_7_out,
       not_8_out, not_9_out, not_10_out;

  or or_1 (s3, op0, op1, op2);
  not not_1 (not_1_out, op5);
  not not_2 (not_2_out, op3);
  not not_3 (not_3_out, op2);
  not not_4 (not_4_out, op1);
  not not_5 (not_5_out, op3);
  not not_6 (not_6_out, op2);
  not not_7 (not_7_out, op4);
  not not_8 (not_8_out, op2);
  not not_9 (not_9_out, op1);
  not not_10 (not_10_out, op0);
  or or_2 (s0, op0, op1);
  and and_1 (s2, not_1_out, not_2_out, not_3_out, not_4_out);
  and and_2 (and_2_out, not_5_out, not_6_out);
  and and_3 (and_3_out, op5, not_7_out, not_8_out, not_9_out, not_10_out);
  or or_3 (s1, and_2_out, and_3_out);
endmodule

module Register_File (
  input  [4:0] A1___Output_0_Address,
  input  [4:0] A2___Output_1_Address,
  input  [4:0] A3___Write_Address,
  input  [31:0] WD3___Write_Value,
  input  CLK___Clock,
  input  WE3___Write_Enable,
  input  clear,
  output [31:0] RD1___Output_0,
  output [31:0] RD2___Output_1
);

  wire decoder_1_out0, decoder_1_out1, decoder_1_out2, decoder_1_out3, decoder_1_out4, decoder_1_out5,
       decoder_1_out6, decoder_1_out7, decoder_1_out8, decoder_1_out9, decoder_1_out10, decoder_1_out11,
       decoder_1_out12, decoder_1_out13, decoder_1_out14, decoder_1_out15, decoder_1_out16, decoder_1_out17,
       decoder_1_out18, decoder_1_out19, decoder_1_out20, decoder_1_out21, decoder_1_out22, decoder_1_out23,
       decoder_1_out24, decoder_1_out25, decoder_1_out26, decoder_1_out27, decoder_1_out28, decoder_1_out29,
       decoder_1_out30, decoder_1_out31;
  wire [31:0] _0___0_q, a0___4_q, a1___5_q, a2___6_q, a3___7_q, at___1_q, fp___30_q, gp___28_q, k0___26_q,
       k1___27_q, ra___31_q, s0___16_q, s1___17_q, s2___18_q, s3___19_q, s4___20_q, s5___21_q, s6___22_q,
       s7___23_q, sp___29_q, t0___8_q, t1___9_q, t2___10_q, t3___11_q, t4___12_q, t5___13_q, t6___14_q,
       t7___15_q, t8___24_q, t9___25_q, v0___2_q, v1___3_q;

  Decoder #(.select(5), .disabled(0)) decoder_1 (
    .out0(decoder_1_out0), .out1(decoder_1_out1), .out2(decoder_1_out2), .out3(decoder_1_out3),
    .out4(decoder_1_out4), .out5(decoder_1_out5), .out6(decoder_1_out6), .out7(decoder_1_out7),
    .out8(decoder_1_out8), .out9(decoder_1_out9), .out10(decoder_1_out10), .out11(decoder_1_out11),
    .out12(decoder_1_out12), .out13(decoder_1_out13), .out14(decoder_1_out14), .out15(decoder_1_out15),
    .out16(decoder_1_out16), .out17(decoder_1_out17), .out18(decoder_1_out18), .out19(decoder_1_out19),
    .out20(decoder_1_out20), .out21(decoder_1_out21), .out22(decoder_1_out22), .out23(decoder_1_out23),
    .out24(decoder_1_out24), .out25(decoder_1_out25), .out26(decoder_1_out26), .out27(decoder_1_out27),
    .out28(decoder_1_out28), .out29(decoder_1_out29), .out30(decoder_1_out30), .out31(decoder_1_out31),
    .sel(A3___Write_Address), .en(WE3___Write_Enable));
  Register #(.width(32)) _0___0 (.D({32{1'b0}}), .en(decoder_1_out0), .Q(_0___0_q), .clk(CLK___Clock), .clr(clear));
  Register #(.width(32)) at___1 (
    .D(WD3___Write_Value), .en(decoder_1_out1), .Q(at___1_q), .clk(CLK___Clock), .clr(clear));
  Register #(.width(32)) v0___2 (
    .D(WD3___Write_Value), .en(decoder_1_out2), .Q(v0___2_q), .clk(CLK___Clock), .clr(clear));
  Register #(.width(32)) v1___3 (
    .D(WD3___Write_Value), .en(decoder_1_out3), .Q(v1___3_q), .clk(CLK___Clock), .clr(clear));
  Register #(.width(32)) a0___4 (
    .D(WD3___Write_Value), .en(decoder_1_out4), .Q(a0___4_q), .clk(CLK___Clock), .clr(clear));
  Register #(.width(32)) a1___5 (
    .D(WD3___Write_Value), .en(decoder_1_out5), .Q(a1___5_q), .clk(CLK___Clock), .clr(clear));
  Register #(.width(32)) a2___6 (
    .D(WD3___Write_Value), .en(decoder_1_out6), .Q(a2___6_q), .clk(CLK___Clock), .clr(clear));
  Register #(.width(32)) a3___7 (
    .D(WD3___Write_Value), .en(decoder_1_out7), .Q(a3___7_q), .clk(CLK___Clock), .clr(clear));
  Register #(.width(32)) t0___8 (
    .D(WD3___Write_Value), .en(decoder_1_out8), .Q(t0___8_q), .clk(CLK___Clock), .clr(clear));
  Register #(.width(32)) t1___9 (
    .D(WD3___Write_Value), .en(decoder_1_out9), .Q(t1___9_q), .clk(CLK___Clock), .clr(clear));
  Register #(.width(32)) t2___10 (
    .D(WD3___Write_Value), .en(decoder_1_out10), .Q(t2___10_q), .clk(CLK___Clock), .clr(clear));
  Register #(.width(32)) t3___11 (
    .D(WD3___Write_Value), .en(decoder_1_out11), .Q(t3___11_q), .clk(CLK___Clock), .clr(clear));
  Register #(.width(32)) t4___12 (
    .D(WD3___Write_Value), .en(decoder_1_out12), .Q(t4___12_q), .clk(CLK___Clock), .clr(clear));
  Register #(.width(32)) t5___13 (
    .D(WD3___Write_Value), .en(decoder_1_out13), .Q(t5___13_q), .clk(CLK___Clock), .clr(clear));
  Register #(.width(32)) t6___14 (
    .D(WD3___Write_Value), .en(decoder_1_out14), .Q(t6___14_q), .clk(CLK___Clock), .clr(clear));
  Register #(.width(32)) t7___15 (
    .D(WD3___Write_Value), .en(decoder_1_out15), .Q(t7___15_q), .clk(CLK___Clock), .clr(clear));
  Register #(.width(32)) s0___16 (
    .D(WD3___Write_Value), .en(decoder_1_out16), .Q(s0___16_q), .clk(CLK___Clock), .clr(clear));
  Register #(.width(32)) s1___17 (
    .D(WD3___Write_Value), .en(decoder_1_out17), .Q(s1___17_q), .clk(CLK___Clock), .clr(clear));
  Register #(.width(32)) s2___18 (
    .D(WD3___Write_Value), .en(decoder_1_out18), .Q(s2___18_q), .clk(CLK___Clock), .clr(clear));
  Register #(.width(32)) s3___19 (
    .D(WD3___Write_Value), .en(decoder_1_out19), .Q(s3___19_q), .clk(CLK___Clock), .clr(clear));
  Register #(.width(32)) s4___20 (
    .D(WD3___Write_Value), .en(decoder_1_out20), .Q(s4___20_q), .clk(CLK___Clock), .clr(clear));
  Register #(.width(32)) s5___21 (
    .D(WD3___Write_Value), .en(decoder_1_out21), .Q(s5___21_q), .clk(CLK___Clock), .clr(clear));
  Register #(.width(32)) s6___22 (
    .D(WD3___Write_Value), .en(decoder_1_out22), .Q(s6___22_q), .clk(CLK___Clock), .clr(clear));
  Register #(.width(32)) s7___23 (
    .D(WD3___Write_Value), .en(decoder_1_out23), .Q(s7___23_q), .clk(CLK___Clock), .clr(clear));
  Register #(.width(32)) t8___24 (
    .D(WD3___Write_Value), .en(decoder_1_out24), .Q(t8___24_q), .clk(CLK___Clock), .clr(clear));
  Register #(.width(32)) t9___25 (
    .D(WD3___Write_Value), .en(decoder_1_out25), .Q(t9___25_q), .clk(CLK___Clock), .clr(clear));
  Register #(.width(32)) k0___26 (
    .D(WD3___Write_Value), .en(decoder_1_out26), .Q(k0___26_q), .clk(CLK___Clock), .clr(clear));
  Register #(.width(32)) k1___27 (
    .D(WD3___Write_Value), .en(decoder_1_out27), .Q(k1___27_q), .clk(CLK___Clock), .clr(clear));
  Register #(.width(32)) gp___28 (
    .D(WD3___Write_Value), .en(decoder_1_out28), .Q(gp___28_q), .clk(CLK___Clock), .clr(clear));
  Register #(.width(32)) sp___29 (
    .D(WD3___Write_Value), .en(decoder_1_out29), .Q(sp___29_q), .clk(CLK___Clock), .clr(clear));
  Register #(.width(32)) fp___30 (
    .D(WD3___Write_Value), .en(decoder_1_out30), .Q(fp___30_q), .clk(CLK___Clock), .clr(clear));
  Register #(.width(32)) ra___31 (
    .D(WD3___Write_Value), .en(decoder_1_out31), .Q(ra___31_q), .clk(CLK___Clock), .clr(clear));
  Multiplexer #(.select(5), .width(32)) multiplexer_1 (
    .in0(_0___0_q), .in1(at___1_q), .in2(v0___2_q), .in3(v1___3_q), .in4(a0___4_q), .in5(a1___5_q),
    .in6(a2___6_q), .in7(a3___7_q), .in8(t0___8_q), .in9(t1___9_q), .in10(t2___10_q), .in11(t3___11_q),
    .in12(t4___12_q), .in13(t5___13_q), .in14(t6___14_q), .in15(t7___15_q), .in16(s0___16_q),
    .in17(s1___17_q), .in18(s2___18_q), .in19(s3___19_q), .in20(s4___20_q), .in21(s5___21_q),
    .in22(s6___22_q), .in23(s7___23_q), .in24(t8___24_q), .in25(t9___25_q), .in26(k0___26_q),
    .in27(k1___27_q), .in28(gp___28_q), .in29(sp___29_q), .in30(fp___30_q), .in31(ra___31_q),
    .out(RD1___Output_0), .sel(A1___Output_0_Address));  // open: en
  Multiplexer #(.select(5), .width(32)) multiplexer_2 (
    .in0(_0___0_q), .in1(at___1_q), .in2(v0___2_q), .in3(v1___3_q), .in4(a0___4_q), .in5(a1___5_q),
    .in6(a2___6_q), .in7(a3___7_q), .in8(t0___8_q), .in9(t1___9_q), .in10(t2___10_q), .in11(t3___11_q),
    .in12(t4___12_q), .in13(t5___13_q), .in14(t6___14_q), .in15(t7___15_q), .in16(s0___16_q),
    .in17(s1___17_q), .in18(s2___18_q), .in19(s3___19_q), .in20(s4___20_q), .in21(s5___21_q),
    .in22(s6___22_q), .in23(s7___23_q), .in24(t8___24_q), .in25(t9___25_q), .in26(k0___26_q),
    .in27(k1___27_q), .in28(gp___28_q), .in29(sp___29_q), .in30(fp___30_q), .in31(ra___31_q),
    .out(RD2___Output_1), .sel(A2___Output_1_Address));  // open: en
endmodule

module ALU_fn (
  input  ALUOp1,
  input  ALUOp0,
  input  Funct5,
  input  Funct4,
  input  Funct3,
  input  Funct2,
  input  Funct1,
  input  Funct0,
  output ALUControl2,
  output ALUControl1,
  output ALUControl0
);

  wire and_1_out, and_2_out, and_3_out, and_4_out, and_5_out, and_6_out, and_7_out, and_8_out, and_9_out,
       and_10_out, not_1_out, not_2_out, not_3_out, not_4_out, not_5_out, not_6_out, not_7_out, not_8_out,
       not_9_out, not_10_out, not_11_out, not_12_out, not_13_out, not_14_out, not_15_out, not_16_out,
       not_17_out, not_18_out, not_19_out, not_20_out, not_21_out, not_22_out, not_23_out, not_24_out,
       not_25_out, not_26_out, not_27_out, not_28_out, not_29_out, not_30_out, not_31_out, not_32_out;

  not not_1 (not_1_out, ALUOp1);
  not not_2 (not_2_out, Funct4);
  not not_3 (not_3_out, Funct3);
  not not_4 (not_4_out, Funct2);
  not not_5 (not_5_out, Funct0);
  not not_6 (not_6_out, Funct4);
  not not_7 (not_7_out, Funct2);
  not not_8 (not_8_out, Funct0);
  not not_9 (not_9_out, Funct4);
  not not_10 (not_10_out, Funct3);
  not not_11 (not_11_out, Funct2);
  not not_12 (not_12_out, Funct0);
  not not_13 (not_13_out, Funct4);
  not not_14 (not_14_out, Funct3);
  not not_15 (not_15_out, Funct0);
  not not_16 (not_16_out, Funct4);
  not not_17 (not_17_out, Funct2);
  not not_18 (not_18_out, Funct0);
  not not_19 (not_19_out, ALUOp0);
  not not_20 (not_20_out, Funct4);
  not not_21 (not_21_out, Funct3);
  not not_22 (not_22_out, Funct0);
  not not_23 (not_23_out, Funct4);
  not not_24 (not_24_out, Funct3);
  not not_25 (not_25_out, Funct1);
  not not_26 (not_26_out, Funct4);
  not not_27 (not_27_out, Funct3);
  not not_28 (not_28_out, Funct0);
  not not_29 (not_29_out, Funct4);
  not not_30 (not_30_out, Funct2);
  not not_31 (not_31_out, Funct0);
  and and_1 (and_1_out, not_1_out, ALUOp0);
  and and_2 (and_2_out, ALUOp1, Funct5, not_2_out, not_3_out, not_4_out, Funct1, not_5_out);
  and and_3 (and_3_out, ALUOp1, Funct5, not_6_out, Funct3, not_7_out, Funct1, not_8_out);
  not not_32 (not_32_out, ALUOp1);
  and and_4 (and_4_out, Funct5, not_9_out, not_10_out, not_11_out, not_12_out);
  and and_5 (and_5_out, Funct5, not_13_out, not_14_out, Funct1, not_15_out);
  and and_6 (and_6_out, Funct5, not_16_out, not_17_out, Funct1, not_18_out);
  and and_7 (and_7_out, not_19_out, Funct5, not_20_out, not_21_out, Funct2, Funct1, not_22_out);
  and and_8 (and_8_out, ALUOp1, Funct5, not_23_out, not_24_out, Funct2, not_25_out, Funct0);
  and and_9 (and_9_out, ALUOp1, Funct5, not_26_out, not_27_out, Funct2, Funct1, not_28_out);
  and and_10 (and_10_out, ALUOp1, Funct5, not_29_out, Funct3, not_30_out, Funct1, not_31_out);
  or or_1 (ALUControl2, and_1_out, and_2_out, and_3_out);
  or or_2 (ALUControl1, not_32_out, and_4_out, and_5_out, and_6_out);
  or or_3 (ALUControl0, and_7_out, and_8_out, and_9_out, and_10_out);
endmodule

module ALU (
  input  [1:0] Aluop,
  input  [5:0] fncd,
  input  [31:0] A,
  input  [31:0] B,
  output IntCause,
  output EPCWrite,
  output CauseWrite,
  output [31:0] Output,
  output Equal_Flag
);

  wire adder_1_cout, bit_extender_1_out, bit_extender_2_out, bit_extender_4_out, bit_extender_5_out,
       comparator_1_lt, DiffOverflow, multiplexer_1_out, multiplexer_2_out, not_1_out, subtractor_1_bout,
       SumOverflow, xor_1_out, xor_3_out, xor_4_out;
  wire [2:0] alu_fn_1_alucontrol0;
  wire [31:0] adder_1_out, and_1_out, bit_extender_3_out, or_1_out, shifter_1_out, shifter_2_out,
       shifter_3_out, shifter_4_out, subtractor_1_out, xor_2_out;

  ALU_fn alu_fn_1 (
    .ALUOp1(Aluop[1]), .ALUOp0(Aluop[0]), .Funct5(fncd[5]), .Funct4(fncd[4]), .Funct3(fncd[3]),
    .Funct2(fncd[2]), .Funct1(fncd[1]), .Funct0(fncd[0]), .ALUControl2(alu_fn_1_alucontrol0[2]),
    .ALUControl1(alu_fn_1_alucontrol0[1]), .ALUControl0(alu_fn_1_alucontrol0[0]));
  Shifter #(.width(32), .shift("lr")) shifter_1 (.in(A), .\dist ({5{1'b1}}), .out(shifter_1_out));
  Shifter #(.width(32), .shift("lr")) shifter_2 (.in(B), .\dist ({5{1'b1}}), .out(shifter_2_out));
  Bit_Extender #(.in_width(32), .out_width(1), .\type ("sign")) bit_extender_1 (
    .in(shifter_1_out), .out(bit_extender_1_out));
  Bit_Extender #(.in_width(32), .out_width(1), .\type ("sign")) bit_extender_2 (
    .in(shifter_2_out), .out(bit_extender_2_out));
  assign and_1_out = A & B;  // AND_Gate and_1, 32 bits wide
  assign or_1_out = A | B;  // OR_Gate or_1, 32 bits wide
  Adder #(.width(32)) adder_1 (.a(A), .b(B), .out(adder_1_out), .cout(adder_1_cout));  // open: cin
  Subtractor #(.width(32)) subtractor_1 (.a(A), .b(B), .out(subtractor_1_out), .bout(subtractor_1_bout));  // open: bin
  Comparator #(.width(32)) comparator_1 (.a(A), .b(B), .eq(Equal_Flag), .lt(comparator_1_lt));  // open: gt
  xor xor_1 (xor_1_out, bit_extender_1_out, bit_extender_2_out);
  assign xor_2_out = B ^ A;  // XOR_Gate xor_2, 32 bits wide
  xor xor_3 (xor_3_out, SumOverflow, xor_1_out);
  xor xor_4 (xor_4_out, xor_1_out, DiffOverflow);
  assign bit_extender_3_out = {{31{1'b0}}, comparator_1_lt};  // Bit_Extender bit_extender_3
  Shifter #(.width(32), .shift("lr")) shifter_3 (.in(adder_1_out), .\dist (5'b11001), .out(shifter_3_out));
  Shifter #(.width(32), .shift("lr")) shifter_4 (.in(subtractor_1_out), .\dist (5'b11001), .out(shifter_4_out));
  Multiplexer #(.select(3)) multiplexer_1 (
    .in0(1'b0), .in1(1'b0), .in2(1'b0), .in3(1'b0), .in4(1'b1), .in5(1'b1), .in6(1'b0), .in7(1'b0),
    .out(multiplexer_1_out), .sel(alu_fn_1_alucontrol0));  // open: en
  Multiplexer #(.select(3)) multiplexer_2 (
    .in0(1'b0), .in1(1'b0), .in2(xor_3_out), .in3(1'b0), .in4(1'b0), .in5(1'b0), .in6(xor_4_out), .in7(1'b0),
    .out(multiplexer_2_out), .sel(alu_fn_1_alucontrol0));  // open: en
  Multiplexer #(.select(3), .width(32), .disabled(0), .enable("false")) multiplexer_3 (
    .in0(and_1_out), .in1(or_1_out), .in2(adder_1_out), .in3(xor_2_out), .in6(subtractor_1_out),
    .in7(bit_extender_3_out), .out(Output), .sel(alu_fn_1_alucontrol0));  // open: in4, in5
  Bit_Extender #(.in_width(32), .out_width(1), .\type ("sign")) bit_extender_4 (
    .in(shifter_3_out), .out(bit_extender_4_out));
  Bit_Extender #(.in_width(32), .out_width(1), .\type ("sign")) bit_extender_5 (
    .in(shifter_4_out), .out(bit_extender_5_out));
  not not_1 (not_1_out, multiplexer_2_out);
  xor xor_5 (SumOverflow, bit_extender_4_out, adder_1_cout);
  xor xor_6 (DiffOverflow, bit_extender_5_out, subtractor_1_bout);
  and and_2 (IntCause, multiplexer_1_out, not_1_out);
  or or_2 (EPCWrite, multiplexer_1_out, multiplexer_2_out);
  or or_3 (CauseWrite, multiplexer_1_out, multiplexer_2_out);
endmodule

module control_unit (
  input  op_1,
  input  op_2,
  input  op_3,
  input  op_4,
  input  op_5,
  input  op_6,
  output out_1,
  output out_2,
  output out_3,
  output out_4
);

  wire and_1_out, and_2_out, and_3_out, and_4_out, and_5_out, and_6_out, and_7_out, and_8_out, and_9_out,
       and_10_out, and_11_out, and_12_out, and_13_out, not_1_out, not_2_out, not_3_out, not_4_out, not_5_out,
       not_6_out, not_7_out, not_8_out, not_9_out, not_10_out, not_11_out, not_12_out, not_13_out,
       not_14_out, not_15_out;

  not not_1 (not_1_out, op_6);
  not not_2 (not_2_out, op_5);
  not not_3 (not_3_out, op_3);
  not not_4 (not_4_out, op_4);
  not not_5 (not_5_out, op_5);
  not not_6 (not_6_out, op_5);
  not not_7 (not_7_out, op_1);
  not not_8 (not_8_out, op_2);
  not not_9 (not_9_out, op_6);
  not not_10 (not_10_out, op_3);
  not not_11 (not_11_out, op_4);
  not not_12 (not_12_out, op_3);
  not not_13 (not_13_out, op_4);
  not not_14 (not_14_out, op_6);
  not not_15 (not_15_out, op_6);
  and and_1 (and_1_out, op_5, not_1_out);
  and and_2 (and_2_out, op_3, not_2_out);
  and and_3 (and_3_out, not_3_out, not_4_out, not_5_out);
  and and_4 (and_4_out, not_6_out, op_6);
  and and_5 (and_5_out, not_7_out, not_8_out, op_3, op_4, op_5, not_9_out);
  and and_6 (and_6_out, not_10_out, not_11_out);
  and and_7 (and_7_out, not_12_out, op_5);
  and and_8 (and_8_out, not_13_out, op_5);
  and and_9 (and_9_out, op_5, op_6);
  and and_10 (and_10_out, op_2, op_5);
  and and_11 (and_11_out, op_1, op_5);
  and and_12 (and_12_out, op_5, not_14_out);
  and and_13 (and_13_out, op_3, not_15_out);
  or or_1 (out_1, and_1_out, op_4, and_2_out);
  or or_2 (out_2, and_3_out, and_4_out, and_5_out);
  or or_3 (out_3, and_6_out, and_7_out, and_8_out, and_9_out, and_10_out, and_11_out);
  or or_4 (out_4, and_12_out, and_13_out);
endmodule
